# Fritzing sketch CDT (saved by Fritzing 0.9.3b)
breadboards: 1

parts:
  Part1 = HX711 Weighing Sensor Module
  Load_Cell1 = Load Cell - Red/white/black/green
  Part3 = Arduino Nano (Rev3.0) (ICSP)
  LCD1 = LCD screen
  LCM1602_IIC1 = LCM1602 IIC [part_number="LCM1602 IIC" chip_label="LCM1602 IIC" package="DIP (Dual Inline) [THT]"]
  DFPlayer_Mini1 = DFPlayer MINI [package="DIP (Dual Inline) [THT]"]
  SPKR1 = Loudspeaker  # not connected
  S1 = Round Pushbutton

nets:
  VCC: Part1.VCC, Part3.5V, LCM1602_IIC1.VCC, DFPlayer_Mini1.VCC
  GND: Part1.GND, Part3.GND, DFPlayer_Mini1.GND, S1.leg0
  N1: Part1.DO/RX, Part3.D4
  N2: Part1.CK/TX, Part3.D5
  N3: Part1.E+, Load_Cell1.wire1
  N4: Part1.E-, Load_Cell1.wire3
  N5: Part1.A+, Load_Cell1.wire2
  N6: Part1.A-, Load_Cell1.wire4
  N7: Part3.D7, Part3.3V3, S1.leg1
  N8: Part3.D10, DFPlayer_Mini1.RX
  N9: Part3.D11/MOSI, DFPlayer_Mini1.TX
  N10: Part3.A5, LCM1602_IIC1.SCL
  N11: Part3.A4, LCM1602_IIC1.SDA
  VSS: LCD1.VSS, LCM1602_IIC1.VSS
  VDD: LCD1.VDD, LCM1602_IIC1.VDD
  N12: LCD1.V0, LCM1602_IIC1.V0
  N13: LCD1.RS, LCM1602_IIC1.RS
  N14: LCD1.R/W, LCM1602_IIC1.RW
  N15: LCD1.E, LCM1602_IIC1.E
  N16: LCD1.DB0, LCM1602_IIC1.D0
  N17: LCD1.DB1, LCM1602_IIC1.D1
  N18: LCD1.DB2, LCM1602_IIC1.D2
  N19: LCD1.DB3, LCM1602_IIC1.D3
  N20: LCD1.DB4, LCM1602_IIC1.D4
  N21: LCD1.DB5, LCM1602_IIC1.D5
  N22: LCD1.DB6, LCM1602_IIC1.D6
  N23: LCD1.DB7, LCM1602_IIC1.D7
  N24: LCD1.LED+, LCM1602_IIC1.A
  N25: LCD1.LED-, LCM1602_IIC1.K

custom parts:
  Load Cell - Red/white/black/green: A rectangle load cell/weighting pressure Sensor with four wires - Red, white, black, green. Normally corresponding with E+, E-, A+, A- respectively.
  LCM1602 IIC: I2C-Module to use a 1602 or 2004 LCD on with the wire.h libory Serial LCD Modul
  DFPlayer MINI: MP3 module by DFRobot.com for playing Music from an SD-Card. Supports WAV and MP3 files.
